// Logisim project ShadowCircuit.circ as structural Verilog: 1 circuit, main circuit main
module main (
  input  RESET,
  input  ROMDIS
);

  wire MREQ_out, nand_1_out, nand_2_out, or_1_out, or_2_out, RD_out;

  nand nand_1 (nand_1_out, RESET, nand_2_out);
  nand nand_2 (nand_2_out, nand_1_out, ROMDIS);
  Clock RD (.out(RD_out));
  Clock MREQ (.out(MREQ_out));
  or or_1 (or_1_out, RD_out, nand_1_out);
  LED #(.active("false")) RAMOE (.in(or_1_out));
  or or_2 (or_2_out, nand_2_out, MREQ_out);
  LED #(.active("false")) ROMCS (.in(or_2_out));

  // Notes on the sheet:
  //   RESET: pull=up, initial=0x1
  //   ROMDIS: pull=up, initial=0x1
  //   RAMSEL
  //   ROMSEL
endmodule
