// Logisim project Ep2_QuadratureClock.circ as structural Verilog: 1 circuit, main circuit main
module main (
);

  wire j_k_ff_1_q, j_k_ff_1_qn, j_k_ff_2_q, j_k_ff_2_qn, Oscillator_out, Scope_p2, Scope_p3;

  Clock Oscillator (.out(Oscillator_out));
  J_K_Flip_Flop j_k_ff_1 (
    .J(j_k_ff_2_qn), .K(j_k_ff_2_q), .clk(Oscillator_out), .Q(j_k_ff_1_q), .Qn(j_k_ff_1_qn), .preset(1'b0),
    .reset(1'b0));
  J_K_Flip_Flop j_k_ff_2 (
    .J(j_k_ff_1_q), .K(j_k_ff_1_qn), .clk(Oscillator_out), .Q(j_k_ff_2_q), .Qn(j_k_ff_2_qn), .preset(1'b0),
    .reset(1'b0));
  // Digital_Oscilloscope Scope: pin names not known; wires that end beside it: Oscillator_out, Scope_p2, Scope_p3
  not E (Scope_p2, j_k_ff_2_qn);
  not Q (Scope_p3, j_k_ff_1_qn);

  // Notes on the sheet:
  //   Quadrature Clock
  //   74HCT112
  //   74HCT14
endmodule
