// Logisim project Ep3_QuadratureClockWithStretching.circ as structural Verilog: 1 circuit, main circuit main
module main (
  input  MRDY
);

  wire Clock4x_out, d_ff_1_qn, digital_oscilloscope_1_p2, digital_oscilloscope_1_p3, j_k_ff_1_q, j_k_ff_1_qn,
       j_k_ff_2_q, j_k_ff_2_qn, nand_1_out, not_1_out;

  not not_1 (not_1_out, MRDY);
  Clock Clock4x (.out(Clock4x_out));
  D_Flip_Flop d_ff_1 (.D(nand_1_out), .clk(Clock4x_out), .Qn(d_ff_1_qn), .preset(1'b0), .reset(1'b0));  // open: Q
  nand nand_1 (nand_1_out, j_k_ff_1_qn, not_1_out, j_k_ff_2_q);
  J_K_Flip_Flop j_k_ff_1 (
    .J(j_k_ff_2_qn), .K(j_k_ff_2_q), .clk(Clock4x_out), .Q(j_k_ff_1_q), .Qn(j_k_ff_1_qn), .preset(1'b0),
    .reset(d_ff_1_qn));
  J_K_Flip_Flop j_k_ff_2 (
    .J(j_k_ff_1_q), .K(j_k_ff_1_qn), .clk(Clock4x_out), .Q(j_k_ff_2_q), .Qn(j_k_ff_2_qn), .preset(d_ff_1_qn),
    .reset(1'b0));
  // Digital_Oscilloscope #(.frontlines("both"), .nState(9)) digital_oscilloscope_1: pin names not known; wires that end beside it: Clock4x_out, digital_oscilloscope_1_p2, digital_oscilloscope_1_p3
  not E (digital_oscilloscope_1_p2, j_k_ff_2_qn);
  not Q (digital_oscilloscope_1_p3, j_k_ff_1_qn);

  // Notes on the sheet:
  //   MRDY: pull=up, initial=0x1
  //   74HCT74
  //   Note: Set and Reset on the
  //   flip flops are inverted, so
  //   !Q is used instead of Q
  //    on the 74HCT74 chip.
  //   74HCT112
  //   Stretch
  //   74HCT14
  //   Quadrature Clock
endmodule
