// Logisim project Ep5_MMU_Concept.circ as structural Verilog: 1 circuit, main circuit MMU
module MMU (
  input  [15:0] ADDR,
  input  [7:0] DATA,
  input  MMU_TASK,
  input  MMU_EN,
  input  MMU_CONST,
  input  MMU_CS,
  input  RW
);

  wire and_1_out, and_2_out, and_3_out, and_4_out, and_5_out, and_6_out, and_7_out, and_8_out, and_9_out,
       n74245_1_pin10, n74245_1_pin20, not_1_out, not_2_out, not_3_out, not_4_out, not_5_out, not_6_out,
       not_7_out, or_1_out, or_2_out, or_3_out, or_4_out;
  wire [0:0] multiplexer_5_out;
  wire [3:0] multiplexer_1_out, multiplexer_8_out;
  wire [3:1] multiplexer_12_out;
  wire [7:0] controlled_buffer_1_out, MMU_BANK_REGISTERS_data;

  assign controlled_buffer_1_out = not_1_out ? DATA : 8'bz;  // Controlled_Buffer controlled_buffer_1
  not not_1 (not_1_out, or_2_out);
  not not_2 (not_2_out, MMU_EN);
  not not_3 (not_3_out, MMU_CONST);
  not not_4 (not_4_out, MMU_CS);
  not not_5 (not_5_out, RW);
  Multiplexer multiplexer_1 (.in0(ADDR[0]), .in1(ADDR[13]), .out(multiplexer_1_out[0]), .sel(MMU_EN));
  Multiplexer multiplexer_2 (.in0(ADDR[1]), .in1(ADDR[14]), .out(multiplexer_1_out[1]), .sel(MMU_EN));
  Multiplexer multiplexer_3 (.in0(ADDR[2]), .in1(ADDR[15]), .out(multiplexer_1_out[2]), .sel(MMU_EN));
  Multiplexer multiplexer_4 (.in0(ADDR[3]), .in1(MMU_TASK), .out(multiplexer_1_out[3]), .sel(MMU_EN));
  or or_1 (or_1_out, MMU_CS, MMU_CONST);
  or or_2 (or_2_out, RW, MMU_CS, MMU_CONST);
  and and_1 (and_1_out, not_3_out, MMU_CS);
  and and_2 (and_2_out, MMU_CONST, not_4_out);
  and and_3 (and_3_out, not_2_out, not_5_out);
  and and_4 (and_4_out, not_2_out, MMU_CS);
  and and_5 (and_5_out, not_3_out, not_5_out);
  and and_6 (and_6_out, not_3_out, MMU_CS);
  and and_7 (and_7_out, MMU_CONST, not_4_out);
  and and_8 (and_8_out, not_2_out, MMU_CS);
  and and_9 (and_9_out, MMU_EN, MMU_CONST);
  not not_6 (not_6_out, or_2_out);
  not not_7 (not_7_out, or_3_out);
  // Probe on controlled_buffer_1_out
  or or_3 (or_3_out, and_1_out, and_2_out, and_3_out, and_4_out, and_5_out);
  or or_4 (or_4_out, and_6_out, and_7_out, and_8_out);
  RAM #(.addrWidth(4), .databus("bidir"), .enables("line"), .trigger("low"), .\type ("nonvolatile")) MMU_BANK_REGISTERS (
    .addr(multiplexer_1_out), .we(not_6_out), .oe(not_7_out), .clk(or_4_out), .data(MMU_BANK_REGISTERS_data));
  _74245 #(.ShowInternalStructure("true"), .VccGndPorts("true")) u_74245_1 (
    .pin1(RW), .pin2(MMU_BANK_REGISTERS_data[0]), .pin3(MMU_BANK_REGISTERS_data[1]),
    .pin4(MMU_BANK_REGISTERS_data[2]), .pin5(MMU_BANK_REGISTERS_data[3]), .pin6(MMU_BANK_REGISTERS_data[4]),
    .pin7(MMU_BANK_REGISTERS_data[5]), .pin8(MMU_BANK_REGISTERS_data[6]), .pin9(MMU_BANK_REGISTERS_data[7]),
    .pin10(n74245_1_pin10), .pin20(n74245_1_pin20), .pin19(or_1_out), .pin18(controlled_buffer_1_out[0]),
    .pin17(controlled_buffer_1_out[1]), .pin16(controlled_buffer_1_out[2]),
    .pin15(controlled_buffer_1_out[3]), .pin14(controlled_buffer_1_out[4]),
    .pin13(controlled_buffer_1_out[5]), .pin12(controlled_buffer_1_out[6]), .pin11(controlled_buffer_1_out[7]));
  Multiplexer multiplexer_5 (.in0(1'b0), .in1(MMU_BANK_REGISTERS_data[7]), .out(multiplexer_5_out[0]), .sel(and_9_out));
  Multiplexer multiplexer_6 (.in0(1'b0), .in1(MMU_BANK_REGISTERS_data[6]), .out(multiplexer_8_out[3]), .sel(and_9_out));
  Multiplexer multiplexer_7 (.in0(1'b0), .in1(MMU_BANK_REGISTERS_data[5]), .out(multiplexer_8_out[2]), .sel(and_9_out));
  Multiplexer multiplexer_8 (.in0(1'b0), .in1(MMU_BANK_REGISTERS_data[4]), .out(multiplexer_8_out[1]), .sel(and_9_out));
  Multiplexer multiplexer_9 (.in0(1'b0), .in1(MMU_BANK_REGISTERS_data[3]), .out(multiplexer_8_out[0]), .sel(and_9_out));
  Multiplexer multiplexer_10 (
    .in0(ADDR[15]), .in1(MMU_BANK_REGISTERS_data[2]), .out(multiplexer_12_out[3]), .sel(and_9_out));
  Multiplexer multiplexer_11 (
    .in0(ADDR[14]), .in1(MMU_BANK_REGISTERS_data[1]), .out(multiplexer_12_out[2]), .sel(and_9_out));
  Multiplexer multiplexer_12 (
    .in0(ADDR[13]), .in1(MMU_BANK_REGISTERS_data[0]), .out(multiplexer_12_out[1]), .sel(and_9_out));
  Hex_Digit_Display #(.decimalPoint("false")) hex_digit_display_1 (.value({3'b000, multiplexer_5_out[0]}));
  Hex_Digit_Display #(.decimalPoint("false")) hex_digit_display_2 (.value(multiplexer_8_out));
  Hex_Digit_Display #(.decimalPoint("false")) hex_digit_display_3 (.value({multiplexer_12_out, ADDR[12]}));
  Hex_Digit_Display #(.decimalPoint("false")) hex_digit_display_4 (.value(ADDR[11:8]));
  Hex_Digit_Display #(.decimalPoint("false")) hex_digit_display_5 (.value(ADDR[7:4]));
  Hex_Digit_Display #(.decimalPoint("false")) hex_digit_display_6 (.value(ADDR[3:0]));
  Hex_Digit_Display #(.decimalPoint("false")) hex_digit_display_7 (.value({multiplexer_5_out[0], multiplexer_8_out[3:1]}));
  Hex_Digit_Display #(.decimalPoint("false")) hex_digit_display_8 (.value({multiplexer_8_out[0], multiplexer_12_out}));
  // also tied to GND on the sheet: n74245_1_pin10
  // also tied to VCC on the sheet: n74245_1_pin20

  // Notes on the sheet:
  //   ADDR: initial=0xa002
  //   DATA: initial=0x85
  //   MMU_TASK: pull=up
  //   $FF91
  //   $FF90
  //   $FE00-$FFFF
  //   $FFA0-$FFAF
endmodule
