// Logisim project Ep6_MMU_Concept_V4.circ as structural Verilog: 3 circuits, main circuit MAIN
module MAIN (
  input  [15:0] ADDRESS,
  input  [7:0] DATA,
  input  RW
);

  wire address_decode_1_const_cs, address_decode_1_mmu_en, address_decode_1_mmu_reg_cs,
       address_decode_1_mmu_task, not_1_out, not_2_out, not_3_out, not_4_out, pld_logic_1_dir_oe,
       pld_logic_1_mmu_out, pld_logic_1_mux_en, pld_logic_1_ram_en, pld_logic_1_ram_oe, pld_logic_1_ram_w;
  wire [0:0] multiplexer_5_out;
  wire [3:0] multiplexer_1_out, multiplexer_8_out;
  wire [3:1] multiplexer_12_out;
  wire [7:0] controlled_buffer_1_out, MMU_BANK_REGISTERS_data;

  assign controlled_buffer_1_out = not_1_out ? DATA : 8'bz;  // Controlled_Buffer controlled_buffer_1
  not not_1 (not_1_out, pld_logic_1_ram_w);
  // NoConnect on ADDRESS[4]
  // NoConnect on ADDRESS[5]
  // NoConnect on ADDRESS[6]
  // NoConnect on ADDRESS[7]
  // NoConnect on ADDRESS[8]
  // NoConnect on ADDRESS[9]
  // NoConnect on ADDRESS[10]
  // NoConnect on ADDRESS[11]
  // NoConnect on ADDRESS[12]
  // Probe on controlled_buffer_1_out
  ADDRESS_DECODE address_decode_1 (
    .DATA(DATA), .RW(RW), .ADDRESS(ADDRESS), .MMU_EN(address_decode_1_mmu_en),
    .MMU_TASK(address_decode_1_mmu_task), .MMU_REG_CS(address_decode_1_mmu_reg_cs),
    .CONST_CS(address_decode_1_const_cs));
  PLD_LOGIC pld_logic_1 (
    .MMU_EN(address_decode_1_mmu_en), .CS(address_decode_1_mmu_reg_cs), .CONST(address_decode_1_const_cs),
    .RW(RW), .DIR_OE(pld_logic_1_dir_oe), .RAM_W(pld_logic_1_ram_w), .RAM_OE(pld_logic_1_ram_oe),
    .RAM_EN(pld_logic_1_ram_en), .MMU_OUT(pld_logic_1_mmu_out), .MUX_EN(pld_logic_1_mux_en));
  Multiplexer multiplexer_1 (.in0(ADDRESS[0]), .in1(ADDRESS[13]), .out(multiplexer_1_out[0]), .sel(pld_logic_1_mux_en));
  not not_2 (not_2_out, pld_logic_1_ram_oe);
  Multiplexer multiplexer_2 (.in0(ADDRESS[1]), .in1(ADDRESS[14]), .out(multiplexer_1_out[1]), .sel(pld_logic_1_mux_en));
  Multiplexer multiplexer_3 (.in0(ADDRESS[2]), .in1(ADDRESS[15]), .out(multiplexer_1_out[2]), .sel(pld_logic_1_mux_en));
  Multiplexer multiplexer_4 (
    .in0(ADDRESS[3]), .in1(address_decode_1_mmu_task), .out(multiplexer_1_out[3]), .sel(pld_logic_1_mux_en));
  RAM #(.addrWidth(4), .databus("bidir"), .enables("line"), .trigger("high")) MMU_BANK_REGISTERS (
    .addr(multiplexer_1_out), .data(MMU_BANK_REGISTERS_data));  // open: we, oe, clk
  not not_3 (not_3_out, pld_logic_1_ram_w);
  not not_4 (not_4_out, pld_logic_1_ram_en);
  _74245 #(.ShowInternalStructure("true")) u_74245_1 (
    .pin1(RW), .pin2(MMU_BANK_REGISTERS_data[0]), .pin3(MMU_BANK_REGISTERS_data[1]),
    .pin4(MMU_BANK_REGISTERS_data[2]), .pin5(MMU_BANK_REGISTERS_data[3]), .pin6(MMU_BANK_REGISTERS_data[4]),
    .pin7(MMU_BANK_REGISTERS_data[5]), .pin8(MMU_BANK_REGISTERS_data[6]), .pin9(MMU_BANK_REGISTERS_data[7]),
    .pin19(pld_logic_1_dir_oe), .pin18(controlled_buffer_1_out[0]), .pin17(controlled_buffer_1_out[1]),
    .pin16(controlled_buffer_1_out[2]), .pin15(controlled_buffer_1_out[3]),
    .pin14(controlled_buffer_1_out[4]), .pin13(controlled_buffer_1_out[5]),
    .pin12(controlled_buffer_1_out[6]), .pin11(controlled_buffer_1_out[7]));
  Multiplexer multiplexer_5 (
    .in0(1'b0), .in1(MMU_BANK_REGISTERS_data[7]), .out(multiplexer_5_out[0]), .sel(pld_logic_1_mmu_out));
  Multiplexer multiplexer_6 (
    .in0(1'b0), .in1(MMU_BANK_REGISTERS_data[6]), .out(multiplexer_8_out[3]), .sel(pld_logic_1_mmu_out));
  Multiplexer multiplexer_7 (
    .in0(1'b0), .in1(MMU_BANK_REGISTERS_data[5]), .out(multiplexer_8_out[2]), .sel(pld_logic_1_mmu_out));
  Multiplexer multiplexer_8 (
    .in0(1'b0), .in1(MMU_BANK_REGISTERS_data[4]), .out(multiplexer_8_out[1]), .sel(pld_logic_1_mmu_out));
  Multiplexer multiplexer_9 (
    .in0(1'b0), .in1(MMU_BANK_REGISTERS_data[3]), .out(multiplexer_8_out[0]), .sel(pld_logic_1_mmu_out));
  Multiplexer multiplexer_10 (
    .in0(ADDRESS[15]), .in1(MMU_BANK_REGISTERS_data[2]), .out(multiplexer_12_out[3]),
    .sel(pld_logic_1_mmu_out));
  Multiplexer multiplexer_11 (
    .in0(ADDRESS[14]), .in1(MMU_BANK_REGISTERS_data[1]), .out(multiplexer_12_out[2]),
    .sel(pld_logic_1_mmu_out));
  Multiplexer multiplexer_12 (
    .in0(ADDRESS[13]), .in1(MMU_BANK_REGISTERS_data[0]), .out(multiplexer_12_out[1]),
    .sel(pld_logic_1_mmu_out));
  Hex_Digit_Display hex_digit_display_1 (.value({3'b000, multiplexer_5_out[0]}));  // open: dp
  Hex_Digit_Display hex_digit_display_2 (.value(multiplexer_8_out));  // open: dp
  Hex_Digit_Display hex_digit_display_3 (.value({multiplexer_12_out, ADDRESS[12]}));  // open: dp
  Hex_Digit_Display hex_digit_display_4 (.value(ADDRESS[11:8]));  // open: dp
  Hex_Digit_Display hex_digit_display_5 (.value(ADDRESS[7:4]));  // open: dp
  Hex_Digit_Display hex_digit_display_6 (.value(ADDRESS[3:0]));  // open: dp
  Hex_Digit_Display hex_digit_display_7 (.value({multiplexer_5_out[0], multiplexer_8_out[3:1]}));  // open: dp
  Hex_Digit_Display hex_digit_display_8 (.value({multiplexer_8_out[0], multiplexer_12_out}));  // open: dp

  // Notes on the sheet:
  //   RW: pull=down, initial=0x1
  //   ADDRESS: pull=up
endmodule

module ADDRESS_DECODE (
  input  [7:0] DATA,
  input  RW,
  input  [15:0] ADDRESS,
  output MMU_EN,
  output MMU_TASK,
  output MMU_REG_CS,
  output CONST_CS
);

  wire and_1_out, and_2_out, comparator_1_eq, comparator_2_eq, comparator_3_eq, comparator_3_gt,
       comparator_4_eq, comparator_4_lt, comparator_5_eq, comparator_5_gt, comparator_6_eq, comparator_6_lt,
       not_1_out, not_2_out, or_1_out, or_2_out, or_3_out, or_4_out, por_1_out;

  POR #(.PorHighDuration(1)) por_1 (.out(por_1_out));
  not not_1 (not_1_out, RW);
  not not_2 (not_2_out, por_1_out);
  Comparator #(.mode("unsigned"), .width(16)) comparator_1 (
    .a(ADDRESS), .b(16'hff90), .eq(comparator_1_eq));  // open: gt, lt
  Comparator #(.mode("unsigned"), .width(16)) comparator_2 (
    .a(ADDRESS), .b(16'hff91), .eq(comparator_2_eq));  // open: gt, lt
  or or_1 (or_1_out, comparator_3_gt, comparator_3_eq);
  Comparator #(.mode("unsigned"), .width(16)) comparator_3 (
    .a(ADDRESS), .b(16'hffa0), .gt(comparator_3_gt), .eq(comparator_3_eq));  // open: lt
  or or_2 (or_2_out, comparator_4_eq, comparator_4_lt);
  Comparator #(.mode("unsigned"), .width(16)) comparator_4 (
    .a(ADDRESS), .b(16'hffaf), .eq(comparator_4_eq), .lt(comparator_4_lt));  // open: gt
  or or_3 (or_3_out, comparator_5_gt, comparator_5_eq);
  Comparator #(.mode("unsigned"), .width(16)) comparator_5 (
    .a(ADDRESS), .b(16'hfe00), .gt(comparator_5_gt), .eq(comparator_5_eq));  // open: lt
  or or_4 (or_4_out, comparator_6_eq, comparator_6_lt);
  Comparator #(.mode("unsigned"), .width(16)) comparator_6 (
    .a(ADDRESS), .b({16{1'b1}}), .eq(comparator_6_eq), .lt(comparator_6_lt));  // open: gt
  and and_1 (and_1_out, comparator_1_eq, not_1_out);
  and and_2 (and_2_out, not_1_out, comparator_2_eq);
  nand nand_1 (MMU_REG_CS, or_1_out, or_2_out);
  nand nand_2 (CONST_CS, or_3_out, or_4_out);
  _74273 #(.ShowInternalStructure("true")) u_74273_1 (
    .pin1(not_2_out), .pin3(DATA[0]), .pin4(DATA[1]), .pin7(DATA[2]), .pin8(DATA[3]), .pin18(DATA[7]),
    .pin17(DATA[6]), .pin16(MMU_EN), .pin14(DATA[5]), .pin13(DATA[4]), .pin11(and_1_out));  // open: pin2, pin5, pin6, pin9, pin19, pin15, pin12
  _74273 #(.ShowInternalStructure("true")) u_74273_2 (
    .pin1(not_2_out), .pin2(MMU_TASK), .pin3(DATA[0]), .pin4(DATA[1]), .pin7(DATA[2]), .pin8(DATA[3]),
    .pin18(DATA[7]), .pin17(DATA[6]), .pin14(DATA[5]), .pin13(DATA[4]), .pin11(and_2_out));  // open: pin5, pin6, pin9, pin19, pin16, pin15, pin12

  // Notes on the sheet:
  //   RW: initial=0x1
  //   MMU Registers
  //   Constant Range
endmodule

module PLD_LOGIC (
  input  MMU_EN,
  input  CS,
  input  CONST,
  input  RW,
  output DIR_OE,
  output RAM_W,
  output RAM_OE,
  output RAM_EN,
  output MMU_OUT,
  output MUX_EN
);

  wire and_1_out, and_2_out, and_3_out, and_4_out, and_5_out, and_6_out, and_7_out, and_8_out, not_1_out,
       not_2_out, not_3_out, not_4_out;

  not not_1 (not_1_out, MMU_EN);
  not not_2 (not_2_out, CS);
  not not_3 (not_3_out, CONST);
  not not_4 (not_4_out, RW);
  or or_1 (DIR_OE, CONST, CS);
  or or_2 (RAM_W, RW, CONST, CS);
  and and_1 (and_1_out, not_2_out, CONST);
  and and_2 (and_2_out, CS, not_3_out);
  and and_3 (and_3_out, not_1_out, not_4_out);
  and and_4 (and_4_out, not_1_out, CONST);
  and and_5 (and_5_out, not_2_out, not_4_out);
  and and_6 (and_6_out, not_2_out, CONST);
  and and_7 (and_7_out, CS, not_3_out);
  and and_8 (and_8_out, not_1_out, CONST);
  and and_9 (MMU_OUT, MMU_EN, CS, CONST);
  and and_10 (MUX_EN, MMU_EN, CS);
  or or_3 (RAM_OE, and_1_out, and_2_out, and_3_out, and_4_out, and_5_out);
  or or_4 (RAM_EN, and_6_out, and_7_out, and_8_out);
endmodule
